# Fritzing sketch Arduino (saved by Fritzing 0.9.10b)
breadboards: 2

parts:
  S3 = Pushbutton [package="[THT]"]
  R1 = Resistor [tolerance=±5% power=0.25 resistance=2.2k package=THT]
  LED1 = RGB LED (com. cathode, rgb) [package="5 mm [THT]"]
  R8 = Resistor [tolerance=±5% power=0.25 resistance=220 package=THT]
  Q1 = LTR-301 [package=ltr-301]
  S2 = Pushbutton [package="[THT]"]
  J1 = Piezo Speaker
  R2 = Bussed8 Resistor-8 (SIP-9) [tolerance=±5% resistance=10000 package=SIP-9]
  R6 = Resistor [tolerance=±5% power=0.25 resistance=100 package=THT]
  Bauteil1 = Arduino Nano 33 BLE Sense
  R7 = Resistor [tolerance=±5% power=0.25 resistance=220 package=THT]
  SW1 = DIP Switch 8 Position [package=dipswitch-08]
  R9 = Resistor [tolerance=±5% power=0.25 resistance=10k package=THT]
  R10 = Resistor [tolerance=±5% power=0.25 resistance=10k package=THT]
  R11 = Resistor [tolerance=±5% power=0.25 resistance=10k package=THT]
  S1 = Pushbutton [package="[THT]"]
  J4 = male pin header, 4 pins [form="♂ (male)"]
  J5 = male pin header, 3 pins [form="♂ (male)"]

nets:
  N1: S3.Pin_1, S3.Pin_2, Q1.C, S2.Pin_1, S2.Pin_2, Bauteil1.3V3, SW1.9, SW1.10, SW1.11, SW1.12, SW1.13, SW1.14, SW1.15, SW1.16, S1.Pin_1, S1.Pin_2, J4.pin2, J5.pin2
  N2: S3.Pin_3, S3.Pin_4, Bauteil1.D2, R11.Pin_1
  N3: R1.Pin_0, LED1.common_cathode, R8.Pin_1, J1.pin1, R2.Pin_8, Bauteil1.GND, Bauteil1.A7, R9.Pin_0, R10.Pin_0, R11.Pin_0, J4.pin1, J5.pin1
  N4: R1.Pin_1, Q1.E, Bauteil1.A0
  N5: LED1.red_anode, R6.Pin_0
  N6: LED1.green_anode, R7.Pin_0
  N7: LED1.blue_anode, R8.Pin_0
  N8: S2.Pin_3, S2.Pin_4, Bauteil1.D3~, R10.Pin_1
  N9: J1.pin2, Bauteil1.A2
  N10: R2.Pin_0, Bauteil1.D12~/MISO, SW1.1
  N11: R2.Pin_1, Bauteil1.D11/MOSI, Bauteil1.+5V, SW1.2
  N12: R2.Pin_2, Bauteil1.D10~, SW1.3
  N13: R2.Pin_3, Bauteil1.D9~, SW1.4
  N14: R2.Pin_4, Bauteil1.D8, SW1.5
  N15: R2.Pin_5, Bauteil1.D7, SW1.6
  N16: R2.Pin_6, Bauteil1.D6~, SW1.7
  N17: R2.Pin_7, Bauteil1.D5~, SW1.8
  N18: R6.Pin_1, Bauteil1.A3
  N19: Bauteil1.D4, R9.Pin_1, S1.Pin_3, S1.Pin_4
  N20: Bauteil1.A6, R7.Pin_1
  N21: Bauteil1.A5, J4.pin3
  N22: Bauteil1.A4, J4.pin4
  N23: Bauteil1.A1, J5.pin3

custom parts:
  Bussed8 Resistor-8 (SIP-9): A resistor array is a single package which contains more than one resistor. They are typically used for convenience when several resistors are needed together in the same place in a circuit.
  Arduino Nano 33 BLE Sense: The Nano 33 BLE Sense (without headers) is Arduino’s 3.3V AI enabled board in the smallest available form factor: 45x18mm! The Arduino Nano 33 BLE Sense is a completely new board on a well-known form factor. It comes with a series of embedded sensors: 9 axis inertial sensor: what makes this board ideal for wearable devices humidity, and temperature sensor: to get highly accurate measurements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
